# Fritzing sketch AM2320 (saved by Fritzing 0.9.9b)
breadboards: 1

parts:
  M1 = WeMos D1 Mini V3.1.0
  AM1 = AM2320 Humidity and Temperature Sensor [part_number="Adafruit #3721"]
  R1 = Resistor [tolerance=±5% resistance=10k package="0805 [SMD]"]
  R2 = Resistor [tolerance=±5% resistance=10k package="0603 [SMD]"]

nets:
  3V3: M1.3V3, AM1.VDD
  N1: M1.G, AM1.GND, R1.Pin_0, R2.Pin_0
  N2: M1.D2, AM1.SDA, R2.Pin_1
  N3: M1.D1, AM1.SCL, R1.Pin_1

custom parts:
  WeMos D1 Mini V3.1.0: The D1 mini is a mini wifi board based on ESP-8266EX.
  AM2320 Humidity and Temperature Sensor: AM2320 I2C Humidity and Temperature Sensor

// code stored in the sketch: Blink.ino
/*
  Blink

  Turns an LED on for one second, then off for one second, repeatedly.
*/

// the setup function runs once when you press reset or power the board
void setup() {
  // initialize digital pin LED_BUILTIN as an output.
  pinMode(LED_BUILTIN, OUTPUT);
}

// the loop function runs over and over again forever
void loop() {
  digitalWrite(LED_BUILTIN, HIGH);   // turn the LED on (HIGH is the voltage level)
  delay(1000);                       // wait for a second
  digitalWrite(LED_BUILTIN, LOW);    // turn the LED off by making the voltage LOW
  delay(1000);                       // wait for a second
}
